// Logisim project fpu_circuito.circ as structural Verilog: 1 circuit, main circuit main
module main (
  input  Sub,
  input  Sinal,
  input  [7:0] Exp,
  input  [22:0] Mantissa,
  input  Sinal_2,
  input  [7:0] Exp_2,
  input  [22:0] Mantissa_2
);

  wire comparator_1_gt, not_1_out;
  wire [4:0] bitfinder_1_index;
  wire [7:0] adder_1_out, adder_2_out, multiplexer_1_out, subtractor_1_out, subtractor_2_out;
  wire [22:0] multiplexer_2_out, multiplexer_3_out;
  wire [23:0] adder_3_out, multiplexer_4_out, multiplexer_5_out, negator_1_out, negator_2_out, shifter_1_out;

  Adder adder_1 (.a(Exp), .b(8'h7f), .out(adder_1_out));  // open: cin, cout
  Adder adder_2 (.a(Exp_2), .b(8'h7f), .out(adder_2_out));  // open: cin, cout
  Subtractor subtractor_1 (.a(adder_2_out), .b(adder_1_out), .out(subtractor_1_out));  // open: bin, bout
  Subtractor subtractor_2 (.a(adder_1_out), .b(adder_2_out), .out(subtractor_2_out));  // open: bin, bout
  Comparator comparator_1 (.a(adder_1_out), .b(adder_2_out), .gt(comparator_1_gt));  // open: eq, lt
  Multiplexer #(.width(8), .enable("false")) multiplexer_1 (
    .in0(subtractor_1_out), .in1(subtractor_2_out), .out(multiplexer_1_out), .sel(comparator_1_gt));
  not not_1 (not_1_out, comparator_1_gt);
  Multiplexer #(.width(23), .enable("false")) multiplexer_2 (
    .in0(Mantissa), .in1(Mantissa_2), .out(multiplexer_2_out), .sel(not_1_out));
  Multiplexer #(.width(23), .enable("false")) multiplexer_3 (
    .in0(Mantissa), .in1(Mantissa_2), .out(multiplexer_3_out), .sel(comparator_1_gt));
  Shifter #(.width(24), .shift("lr")) shifter_1 (
    .in({1'b1, multiplexer_3_out}), .\dist (multiplexer_1_out[4:0]), .out(shifter_1_out));
  Negator #(.width(24)) negator_1 (.in(shifter_1_out), .out(negator_1_out));
  Multiplexer #(.width(24), .enable("false")) multiplexer_4 (
    .in0(shifter_1_out), .in1(negator_1_out), .out(multiplexer_4_out), .sel(Sub));
  Adder #(.width(24)) adder_3 (
    .a(multiplexer_4_out), .b({1'b1, multiplexer_2_out}), .out(adder_3_out));  // open: cin, cout
  Negator #(.width(24)) negator_2 (.in(adder_3_out), .out(negator_2_out));
  Multiplexer #(.width(24), .enable("false")) multiplexer_5 (
    .in0(adder_3_out), .in1(negator_2_out), .out(multiplexer_5_out), .sel(adder_3_out[23]));
  BitFinder #(.width(24), .\type ("high1")) bitfinder_1 (
    .in(multiplexer_5_out), .index(bitfinder_1_index));  // open: found

  // Notes on the sheet:
  //   A
  //   B-A
  //   A-B
  //   Unidade de ponto flutuante FPU
  //   B
endmodule
